// Digital circuit ControlUnit.dig as structural Verilog
module ControlUnit (
  input  [5:0] Opcode,
  input  Reset,
  output aluSrc,
  output RegDst,
  output [2:0] aluOp,
  output memToReg,
  output memRead,
  output memWrite,
  output RegWrite
);

  wire comparator_1_eq, LW_eq, SW_eq;
  wire [1:0] priorityencoder_1_num;
  wire [8:0] multiplexer_1_out;

  Comparator #(.Bits(6)) comparator_1 (.a(Opcode), .b({6{1'b0}}), .eq(comparator_1_eq));  // open: gt, lt
  Comparator #(.Bits(6)) SW (.a(Opcode), .b(6'b101011), .eq(SW_eq));  // open: gt, lt
  Comparator #(.Bits(6)) LW (.a(Opcode), .b(6'b100011), .eq(LW_eq));  // open: gt, lt
  PriorityEncoder #(.Selector_Bits(2)) priorityencoder_1 (
    .in0(comparator_1_eq), .in1(SW_eq), .in2(LW_eq), .in3(1'b0), .num(priorityencoder_1_num));  // open: any
  Multiplexer #(.Selector_Bits(2), .Bits(9)) multiplexer_1 (
    .sel(priorityencoder_1_num), .in_0(9'h178), .in_1(9'h91), .in_2(9'h196), .in_3({9{1'b0}}),
    .out(multiplexer_1_out));
  Multiplexer #(.Bits(9)) multiplexer_2 (
    .sel(Reset), .in_0(multiplexer_1_out), .in_1({9{1'b0}}),
    .out({RegWrite, aluSrc, RegDst, aluOp, memToReg, memRead, memWrite}));

  // Other names for the same wires on the sheet: rst = Reset

  // Notes on the sheet:
  //   Reset: RESET input
endmodule
