// Digital circuit MIPS32SOC.dig as structural Verilog
module MIPS32SOC (
  input  clk,
  input  rst,
  output invalid_opcode
);

  wire alu_1_iszero, aluSrc, and_1_out, and_2_out, beq, bne, jump, memRead, memToReg, memWrite, not_1_out,
       or_1_out, RegDst, RegWrite;
  wire [2:0] aluFunc, aluOp;
  wire [3:0] add_1_s_2;
  wire [4:0] multiplexer_2_out;
  wire [5:0] Func, Opcode;
  wire [25:6] Inst_Mem_d;
  wire [27:0] add_1_s;
  wire [31:0] add_2_s, alu_1_res, bitextender_1_out, Data_Mem_d, multiplexer_1_out, multiplexer_3_out,
       multiplexer_4_out, multiplexer_5_out, PC_q, Reg_File_da, Reg_File_db, wData;

  Multiplexer #(.Bits(32)) multiplexer_1 (
    .sel(rst), .in_0(multiplexer_5_out), .in_1({32{1'b0}}), .out(multiplexer_1_out));
  Register #(.Bits(32)) PC (.D(multiplexer_1_out), .C(clk), .en(1'b1), .Q(PC_q));
  Add #(.Bits(32)) add_1 (.a(PC_q), .b(32'h4), .c_i(1'b0), .s({add_1_s_2, add_1_s}));  // open: c_o
  ROM #(.AddrBits(8), .Bits(32)) Inst_Mem (.A(PC_q[9:2]), .sel(1'b1), .D({Opcode, Inst_Mem_d, Func}));
  ControlUnit controlunit_1 (
    .rst(rst), .Opcode(Opcode), .memWrite(memWrite), .memRead(memRead), .memToReg(memToReg), .aluOp(aluOp),
    .RegDst(RegDst), .aluSrc(aluSrc), .RegWrite(RegWrite), .beq(beq), .jump(jump), .bne(bne));
  Multiplexer #(.Bits(5)) multiplexer_2 (
    .sel(RegDst), .in_0(Inst_Mem_d[20:16]), .in_1(Inst_Mem_d[15:11]), .out(multiplexer_2_out));
  BitExtender #(.inputBits(16), .outputBits(32)) bitextender_1 (.in({Inst_Mem_d[15:6], Func}), .out(bitextender_1_out));
  RegisterFile #(.AddrBits(5), .Bits(32)) Reg_File (
    .Din(wData), .we(RegWrite), .Rw(multiplexer_2_out), .C(clk), .Ra(Inst_Mem_d[25:21]),
    .Rb(Inst_Mem_d[20:16]), .Da(Reg_File_da), .Db(Reg_File_db));
  Multiplexer #(.Bits(32)) multiplexer_3 (
    .sel(aluSrc), .in_0(Reg_File_db), .in_1(bitextender_1_out), .out(multiplexer_3_out));
  and and_1 (and_1_out, beq, alu_1_iszero);
  Add #(.Bits(32)) add_2 (
    .a({add_1_s_2, add_1_s}), .b({bitextender_1_out[29:0], 2'b00}), .c_i(1'b0), .s(add_2_s));  // open: c_o
  not not_1 (not_1_out, alu_1_iszero);
  ALU alu_1 (.a(Reg_File_da), .b(multiplexer_3_out), .op(aluFunc), .res(alu_1_res), .isZero(alu_1_iszero));
  Multiplexer #(.Bits(32)) multiplexer_4 (
    .sel(or_1_out), .in_0({add_1_s_2, add_1_s}), .in_1(add_2_s), .out(multiplexer_4_out));
  and and_2 (and_2_out, bne, not_1_out);
  Multiplexer #(.Bits(32)) multiplexer_5 (
    .sel(jump), .in_0(multiplexer_4_out), .in_1({add_1_s_2, Inst_Mem_d, Func, 2'b00}), .out(multiplexer_5_out));
  ALUControl alucontrol_1 (.aluOp(aluOp), .Func(Func), .aluFunc(aluFunc));
  or or_1 (or_1_out, and_1_out, and_2_out);
  RAMDualPort #(.AddrBits(8), .Bits(32)) Data_Mem (
    .A(alu_1_res[9:2]), .Din(Reg_File_db), .str(memWrite), .C(clk), .ld(memRead), .D(Data_Mem_d));
  Multiplexer #(.Bits(32)) multiplexer_6 (.sel(memToReg), .in_0(alu_1_res), .in_1(Data_Mem_d), .out(wData));

  assign invalid_opcode = 1'b0;

  // Notes on the sheet:
  //   contents of Inst_Mem (hex, n*v repeats v):
  //   8c080000,8c090004,ac080008
endmodule
