// Digital circuit ControlUnit.dig as structural Verilog
module ControlUnit (
  input  rst,
  input  [5:0] Opcode,
  output memWrite,
  output memRead,
  output memToReg,
  output [2:0] aluOp,
  output RegDst,
  output aluSrc,
  output RegWrite,
  output beq,
  output jump,
  output bne
);

  wire beq_eq, bne_eq, jmp_eq, lui_eq, LW_eq, R_format_eq, SW_eq;
  wire [2:0] priorityencoder_1_num;
  wire [11:0] multiplexer_1_out;

  Comparator #(.Bits(6)) R_format (.a(Opcode), .b({6{1'b0}}), .eq(R_format_eq));  // open: gt, lt
  Comparator #(.Bits(6)) SW (.a(Opcode), .b(6'b101011), .eq(SW_eq));  // open: gt, lt
  Comparator #(.Bits(6)) LW (.a(Opcode), .b(6'b100011), .eq(LW_eq));  // open: gt, lt
  Comparator #(.Bits(6)) u_beq (.a(Opcode), .b(6'b000100), .eq(beq_eq));  // open: gt, lt
  Comparator #(.Bits(6)) u_bne (.a(Opcode), .b(6'b000101), .eq(bne_eq));  // open: gt, lt
  Comparator #(.Bits(6)) jmp (.a(Opcode), .b(6'b000010), .eq(jmp_eq));  // open: gt, lt
  Comparator #(.Bits(6)) lui (.a(Opcode), .b(6'b001111), .eq(lui_eq));  // open: gt, lt
  PriorityEncoder #(.Selector_Bits(3)) priorityencoder_1 (
    .in0(R_format_eq), .in1(SW_eq), .in2(LW_eq), .in3(beq_eq), .in4(bne_eq), .in5(jmp_eq), .in6(lui_eq),
    .in7(1'b0), .num(priorityencoder_1_num));  // open: any
  Multiplexer #(.Selector_Bits(3), .Bits(12)) multiplexer_1 (
    .sel(priorityencoder_1_num), .in_0(12'h178), .in_1(12'h91), .in_2(12'h196), .in_3(12'h218),
    .in_4(12'h418), .in_5(12'h838), .in_6(12'h1b0), .in_7({12{1'b0}}), .out(multiplexer_1_out));
  Multiplexer #(.Bits(12)) multiplexer_2 (
    .sel(rst), .in_0(multiplexer_1_out), .in_1({12{1'b0}}),
    .out({jump, bne, beq, RegWrite, aluSrc, RegDst, aluOp, memToReg, memRead, memWrite}));
endmodule
