// Digital circuit ALU.dig as structural Verilog
module ALU (
  input  [31:0] a,
  input  [31:0] b,
  input  [3:0] op,
  input  clk,
  output [31:0] res,
  output isZero,
  output [31:0] mult_high,
  output [31:0] div_low,
  output [31:0] mult_low
);

  wire [0:0] comparator_1_lt;
  wire [31:0] add_1_s, and_1_out, or_1_out, sub_1_s, xor_1_out;
  wire [63:32] u_Div_div;

  assign and_1_out = a & b;  // And and_1, 32 bits wide
  assign or_1_out = a | b;  // Or or_1, 32 bits wide
  Add #(.Bits(32)) add_1 (.a(a), .b(b), .c_i(1'b0), .s(add_1_s));  // open: c_o
  Sub #(.Bits(32)) sub_1 (.a(a), .b(b), .c_i(1'b0), .s(sub_1_s));  // open: c_o
  Comparator #(.Signed("true"), .Bits(32)) comparator_1 (.a(a), .b(b), .lt(comparator_1_lt[0]));  // open: gt, eq
  assign xor_1_out = a ^ b;  // XOr xor_1, 32 bits wide
  Mul #(.Signed("true"), .Bits(32)) mul_1 (.a(a), .b(b), .mul({mult_high, mult_low}));
  Div #(.applicationType("IVERILOG")) u_Div (.a(a), .b(b), .div({u_Div_div, div_low}));
  Multiplexer #(.Selector_Bits(4), .Bits(32)) multiplexer_1 (
    .sel(op), .in_0(and_1_out), .in_1(or_1_out), .in_2(add_1_s), .in_3(sub_1_s),
    .in_4({{31{1'b0}}, comparator_1_lt[0]}), .in_5(xor_1_out), .in_6({b[15:0], {16{1'b0}}}),
    .in_7({32{1'b0}}), .in_8({32{1'b0}}), .in_9({32{1'b0}}), .in_10({32{1'b0}}), .in_11({32{1'b0}}),
    .in_12({32{1'b0}}), .in_13({32{1'b0}}), .in_14({32{1'b0}}), .in_15({32{1'b0}}), .out(res));
  Comparator #(.Bits(32)) comparator_2 (.a(res), .b({32{1'b0}}), .eq(isZero));  // open: gt, lt

  // Other names for the same wires on the sheet: mux[3:0] = op
endmodule

/* Code of Div:
module Div(
	input [31:0] a,
	input [31:0] b,
	output [63:0] div
);

	assign div = a / b;
endmodule
*/
